# Fritzing sketch PACB SKETCH (saved by Fritzing 1.0.5)
perfboards: 3

parts:
  U7 = 74HC595 [package="DIP16 [THT]"]
  U9 = Header 8 [package=1x08_smd]  # not connected
  D4 = Schottky Diode [part_number=1N5817 package="300 mil [THT]"]  # not connected
  S6 = Pushbutton [package="[THT]"]
  D5 = Schottky Diode [part_number=1N5817 package="300 mil [THT]"]  # not connected
  S7 = Pushbutton [package="[THT]"]
  D6 = Schottky Diode [part_number=1N5817 package="300 mil [THT]"]  # not connected
  S8 = Pushbutton [package="[THT]"]
  U8 = Header 8 [package=1x08_smd]  # not connected
  JP10 = Header 1 [package=1x01_offset]  # not connected
  JP11 = Header 1 [package=1x01_offset]  # not connected
  JP12 = Header 1 [package=1x01_offset]  # not connected
  JP13 = Header 1 [package=1x01_offset]  # not connected
  JP14 = Header 1 [package=1x01_offset]  # not connected
  JP15 = Header 1 [package=1x01_offset]  # not connected
  JP16 = Header 1 [package=1x01_offset]  # not connected
  JP17 = Header 1 [package=1x01_offset]  # not connected
  JP18 = Header 1 [package=1x01_offset]  # not connected
  JP19 = Header 1 [package=1x01_offset]  # not connected
  JP20 = Header 1 [package=1x01_offset]  # not connected
  JP22 = Header 1 [package=1x01_offset]  # not connected
  JP23 = Header 1 [package=1x01_offset]  # not connected
  JP26 = Header 1 [package=1x01_offset]  # not connected
  IC2 = IC, DIP package, 24 pins [chip_label=IC]
  JP27 = Header 1 [package=1x01_offset]  # not connected
  JP29 = Header 1 [package=1x01_offset]  # not connected
  JP30 = Header 1 [package=1x01_offset]  # not connected
  JP32 = Header 1 [package=1x01_offset]  # not connected
  JP33 = Header 1 [package=1x01_offset]  # not connected
  JP34 = Header 1 [package=1x01_offset]  # not connected
  JP35 = Header 1 [package=1x01_offset]  # not connected
  C3 = Electrolytic Capacitor [capacitance=1µF voltage=35V package="100 mil [THT, electrolytic]"]

nets:
  N1: U7.SH_CP, IC2.pin16
  N2: U7.ST_CP, IC2.pin13
  N3: U7.DS, IC2.pin14
  N4: S6.Pin_1, S6.Pin_2
  N5: S6.Pin_3, S6.Pin_4
  N6: S7.Pin_1, S7.Pin_2
  N7: S7.Pin_3, S7.Pin_4
  N8: S8.Pin_1, S8.Pin_2
  N9: S8.Pin_3, S8.Pin_4
  N10: IC2.pin21, C3.-
  N11: IC2.pin23, C3.+
